# Fritzing sketch Skematik (saved by Fritzing 0.9.3b)

parts:
  Part1 = Arduino Pro Mini (3.3V)
  OLED1 = OLED Mono 0.56 inch blue or white
  BAT1 = Battery Holders [package=battery-aa]
  TP1 = TP4056 [chip_label=TP4056 package="DIP (Dual Inline) [THT]"]

nets:
  N1: Part1.A4, OLED1.SDA
  N2: Part1.A5, OLED1.SCL
  N3: Part1.RAW, TP1.pin4
  GND: Part1.GND, OLED1.GND, TP1.pin6
  VCC: Part1.VCC, OLED1.VCC
  N4: BAT1.-, TP1.pin5
  N5: BAT1.+, TP1.pin3

custom parts:
  OLED Mono 0.56 inch blue or white: OLED, I2C 3.3V - 5V Blue and White text versions
  Battery Holders: Battery Holders Various common sizes : AA, AAA, 20mm coin cell and 12mm coin cell.
  TP4056: A DIP stand-in part for whatever IC you want. With 6 pins on a 300mil dual inline package (DIP) footprint.
